# Fritzing sketch FeatherLoRaRemote (saved by Fritzing 0.9.10b)

parts:
  Part12 = OLED Monochrome 128x32 I2C [part_number=931]  # not connected
  Part14 = Adafruit Adalogger FeatherWing [part_number="Adafruit #2922"]
  Part17 = Adafruit Feather M0 RFM9x LoRa [part_number="Adafruit #3178 or #3179"]
  DS5 = DS18B20 1-Wire Temperature Sensor [part_number=DS18B20]
  R17 = Resistor [tolerance=±5% resistance=4.7k power=0.25 package=THT]
  Q3 = NPN-Transistor [part_number=2N2222 package="TO92 [THT]"]
  U9 = Molex Picoblade Series Header [part_number=0532610319 package=Picoblade-53261-0319]
  R19 = Resistor [tolerance=±5% resistance=1k power=0.25 package=THT]
  Part23 = Adafruit BMP280 [part_number="Adafruit #2651"]
  Part24 = Adafruit BMP388 [part_number="Adafruit #3966"]
  Part25 = Adafruit BME280 [part_number="Adafruit #2652"]
  DS7 = DS18B20 1-Wire Temperature Sensor [part_number=DS18B20]
  R20 = Resistor [tolerance=±5% resistance=4.7k power=0.25 package=THT]
  U10 = Molex Picoblade Series Header [part_number=0532610319 package=Picoblade-53261-0319]
  U11 = Honeywell SS451A [chip_label="Hall Effect Sensor" package=THT]
  R21 = Resistor [tolerance=±5% resistance=1k power=0.25 package=THT]
  C2 = Ceramic Capacitor [capacitance=0.1mF voltage=35V package="100 mil [THT, multilayer]"]
  Part26 = Adafruit DS3231 STEMMA QT [part_number="Adafruit #5188"]  # not connected
  Part27 = Adafruit SHT31-D [part_number="Adafruit #2857"]  # not connected

nets:
  +3V3: Part14.+3V3, Part17.+3V3
  GND: Part14.GND, Part17.GND
  N1: Part14.SCK, Part17.SCK
  N2: Part14.MOSI, Part17.MOSI
  N3: Part14.MISO, Part17.MISO
  N4: Part14.SDA, Part17.SDA
  N5: Part14.SCL, Part17.SCL
  N6: Part14.CS, Part17.D10
  N7: Part17.D11, R19.Pin_0
  N8: Part17.D5, U11.pin3, R21.Pin_1
  N9: DS5.GND, U9.1
  N10: DS5.DQ, R17.Pin_0
  N11: DS5.VDD, R17.Pin_1, U9.2
  N12: Q3.B, R19.Pin_1
  GND_2: Part23.GND, Part24.GND, Part25.GND
  VCC: Part23.VCC, Part24.VCC, Part25.VCC
  N13: Part23.SDI/SDA, Part23.CS, Part24.SDI/SDA, Part25.SDI/SDA
  N14: Part23.SCK/SCL, Part24.SCK/SCL, Part25.SCK/SCL
  N15: DS7.GND, U10.1
  N16: DS7.DQ, R20.Pin_0
  N17: DS7.VDD, R20.Pin_1, U10.2
  N18: U11.pin2, C2.0
  N19: R21.Pin_0, C2.1

notes:
  Adafruit LoRa FeatherM0
  3D-PAWS Feather LoRa Remote
  v2025-05-05
  Adafruit OLED 128x32
  Display SSD1306
  I2C 7-bit address 0x3C
  Feather Adalogger Shield
  Pin - D10 SD CS
  Pin - SPI MOSI
  Pin - SPI MISO
  Pin - SPI CLK
  Pin - SDA
  Pin - SCL
  Console Enable Jumper
  Jump Pin D12 to Ground
  DS18B20 Onewire
  Temperature 2
  Pin 1 GND
  Pin 2 DQ
  Pin 3 3.3V
  Soil Moisture Sensor 2
  DF Robot SEN0193
  Pin 1 GND
  Pin 2 3.3V
  Pin 3 Sens
  Optional Soil Moisture Power Control
  Pin D11
  Transistor 2N2222
  Pin 1 Collector - load placed before
  Pin 2 Base - with 1K resistor
  Pin 3 Emitter - tied to ground
  Pinouts
  RST
  3v3
  ARef
  GND
  A0 Soil Moisture Sensor 1
  A1 Dallas Sensor 1wire 1
  A2 Soil Moisture Sensor 2
  A3 Dallas Sensor 1wire 2
  A4 Distance Sensor
  A5 Not in Use
  24 SCK SPI0 Clock- SD/LoRA
  24 MOS SPI0 MOSI - SD/LoRA
  22 MIS SPI0 MISO - SD/LoRA
  0 RX Not in Use
  1 TX Not in Use
  io1
  BAT VBAT
  En - Connect to ground to disable the 3.3v regulator
  USB VBUS
  13 LED
  12 Enable Serial Console - Gound Pin
  11 Enable Soil Moisture 2n2222 or 2N3904
  10 SD CS
  9 Does not behave - not using
  6 Not in Use
  5 Rain Gauge Interrupt (put 10k-50k resistor to gnd, when not using)
  21 SCL i2c - RTC/BMX
  20 SDA i2c - RTC/BMX
  BME288
  Barometic Pressure
  Altitude Sensor
  Temperature
  Humidity
  I2C 7-bit address
  Default = 0x76
  SD0 to GND = 0x77
  BMP388
  Barometic Pressure
  Altitude Sensor
  Temperature
  I2C 7-bit address
  Default = 0x77
  SD0 to GND = 0x76
  BMP280
  Barometic Pressure
  Altitude Sensor
  Temperature
  I2C 7-bit address
  Default = 0x77
  SD0 to GND = 0x76
  R T 3 G
  X X V N
  X X 3 D
  A A 3 G
  2 3 V N
  3 D
  A A 3 G
  4 5 V N
  3 D
  S S 3 G
  C D V N
  L A 3 D
  G 3 S S
  N V D C
  D 3 A L
  G 3 D D
  N V 3 2
  D 3
  G 3 D D
  N V 5 4
  D 3
  G 3 A A
  N V 1 0
  D 3
  Soil Moisture Sensor 1
  DF Robot SEN0193
  Pin 1 GND
  Pin 2 3.3V
  Pin 3 Sens
  DS18B20 Onewire
  Temperature 1
  Pin 1 GND
  Pin 2 DQ
  Pin 3 3.3V
  Rain Gauge (D5)
  SS451A Omnipolar Digital Hall-effect Sensor
  Distance Gauge
  Pin A4
  Adafruit OLED 128x32
  Display SSD1306
  I2C 7-bit address 0x3C<module
  Tinovi Leaf-Wet-I2C
  Leaf Moisture
  I2C address 0x61
  Tinovi PM-WCS-3-I2C
  Soil Moisture
  I2C address 0x63
  Tinovi SOIL-MULTI-5-I2C
  Multi LevelSoil Moisture
  I2C 7 address 0x65
  SHT31 Temperature & Humidy
  I2C address 0x44
  I2C address 0x45 ADR Pin High

custom parts:
  OLED Monochrome 128x32 I2C: These displays are small, only about 1" diagonal, but very readable due to the high contrast of an OLED display. This display is made of 128x32 individual white OLED pixels, each one is turned on or off by the controller chip. Because the display makes its own light, no backlight is required. This reduces the power required to run the OLED and is why the display has such high contrast; we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
  Adafruit Adalogger FeatherWing: This is the Adalogger FeatherWing: it adds both a battery-backed Real Time Clock and micro SD card storage to any Feather main board. This FeatherWing will make it real easy to add datalogging to any of our existing Feathers. You get both an I2C real time clock (PCF8523) with 32KHz crystal and battery backup, and a microSD socket that connects to the SPI port pins (+ extra pin for CS). Tested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
  Adafruit Feather M0 RFM9x LoRa: This is the Adafruit Feather M0 RFM95 LoRa Radio - our take on an microcontroller with a "Long Range (LoRa)" packet radio transceiver with built in USB and battery charging. Its an Adafruit Feather M0 with a 433Mhz or 900MHz radio module cooked in! Great for making wireless networks that are more flexible than Bluetooth LE and without the high power requirements of WiFi. We have other boards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
  Adafruit BMP280: Bosch has stepped up their game with their new BMP280 sensor, an environmental sensor with temperature, barometric pressure that is the next generation upgrade to the BMP085/BMP180/BMP183. This sensor is great for all sorts of weather sensing and can even be used in both I2C and SPI! This precision sensor from Bosch is the best low-cost, precision sensing solution for measuring barometric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
  Adafruit BMP388: Bosch has been a leader in barometric pressure sensors, from the BMP085. BMP180, and BMP280... now we've got the next generation, the Adafruit BMP388 Precision Barometric Pressure sensor. As you would expect, this sensor is similar to its earlier versions but even better. The BMP388 has better precision than ever, which makes it excellent for environmental sensing or as a precision altimeter.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
  Adafruit BME280: Bosch has stepped up their game with their new BME280 sensor, an environmental sensor with temperature, barometric pressure and humidity! This sensor is great for all sorts of indoor environmental sensing and can even be used in both I2C and SPI! This precision sensor from Bosch is the best low-cost sensing solution for measuring humidity with ±3% accuracy, barometric pressure with ±1 hPa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
  Honeywell SS451A: Omnipolar Digital Hall-effect Sensor
  Adafruit DS3231 STEMMA QT: The datasheet for the DS3231 explains that this part is an "Extremely Accurate I²C-Integrated RTC/TCXO/Crystal". And, hey, it does exactly what it says on the tin! This Real Time Clock (RTC) is the most precise you can get in a small, low-power package. We've had a breakout board version of this RTC for a while, but we want to make it even easier for folks to use, so now it comes with STEMMA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
  Adafruit SHT31-D: Sensirion Temperature/Humidity sensors are some of the finest & highest-accuracy devices you can get. And, finally we have some that have a true I2C interface for easy reading. The SHT31-D sensor has an excellent ±2% relative humidity and ±0.3°C accuracy for most uses. We now use the version with a PTFE filter, it'll stay clean while still allowing humidity measurements to work Unlike earlier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
